// Logisim project Project1_1110_cam - Copy.circ as structural Verilog: 21 circuits, main circuit main
// IF/ID
module main (
);

  wire ALU_zero, button_1_out, clock_1_out, Decoder_halt, Decoder_immtoalu, Decoder_immtopc, Decoder_led,
       Decoder_memread, Decoder_memtoreg, Decoder_memwrite, Decoder_pctoreg, Decoder_regtopc,
       Decoder_regwrite, Decoder_shiftertoreg, Decoder_shiftsrc, Decoder_writeled, Decoder_zerostoalu,
       ID_EX_memread_2, ID_EX_memwrite_2, ID_EX_subop_2, Instruction_Splitter_subop,
       Instruction_Splitter_unsigned, not_1_out, ResultToLess_less;
  wire [2:0] Instruction_Splitter_read_register1, Instruction_Splitter_read_register2,
       Instruction_Splitter_write_register;
  wire [3:0] Decoder_aluop, ID_EX_aluop_2, ID_EX_shamt_2, Instruction_Splitter_opcode,
       Instruction_Splitter_shift_amount;
  wire [7:0] adder_1_out, IF_ID_pc_out, Instruction_Splitter_immediate, multiplexer_3_out, multiplexer_4_out,
       PC_q, RegisterToAddress_2_address, RegisterToAddress_address;
  wire [15:0] ALU_result, bit_extender_1_out, ID_EX_imm_ext_2, ID_EX_readdata1_2, ID_EX_readdata2_2,
       IF_ID_output_instruction, multiplexer_1_out, multiplexer_2_out, multiplexer_5_out, multiplexer_6_out,
       multiplexer_7_out, ram_1_data, register_1_q, Registers_File_read_data1, Registers_File_read_data2,
       rom_1_data, Shifter_shiftout, Sign_Extend_sign_extended_imm;

  Clock clock_1 (.out(clock_1_out));
  Register PC (.D(multiplexer_4_out), .en(not_1_out), .Q(PC_q), .clk(clock_1_out), .clr(button_1_out));
  not not_1 (not_1_out, Decoder_halt);
  Button button_1 (.out(button_1_out));
  Adder adder_1 (.a(PC_q), .b(8'h1), .out(adder_1_out));  // open: cin, cout
  IF_ID_Buffer IF_ID (
    .PC(PC_q), .Input_Instruction(rom_1_data), .Clock(clock_1_out), .PC_out(IF_ID_pc_out),
    .Output_Instruction(IF_ID_output_instruction));
  ROM #(.dataWidth(16)) rom_1 (.addr(PC_q), .data(rom_1_data), .sel(1'b1));
  Instruction_Splitter Instruction_Splitter (
    .Instruction(IF_ID_output_instruction), .Opcode(Instruction_Splitter_opcode),
    .Read_Register1(Instruction_Splitter_read_register1),
    .Read_Register2(Instruction_Splitter_read_register2),
    .Write_Register(Instruction_Splitter_write_register), .Shift_Amount(Instruction_Splitter_shift_amount),
    .SubOp(Instruction_Splitter_subop), .Unsigned(Instruction_Splitter_unsigned),
    .Immediate(Instruction_Splitter_immediate));
  Sign_Extend Sign_Extend (
    .Unsigned(Instruction_Splitter_unsigned), .Immediate(Instruction_Splitter_immediate),
    .Sign_Extended_Imm(Sign_Extend_sign_extended_imm));
  ResultToLess ResultToLess (.Result(ALU_result), .Less(ResultToLess_less));
  Decoder Decoder (
    .Opcode(Instruction_Splitter_opcode), .SubOp(Instruction_Splitter_subop), .Zero(ALU_zero),
    .Less(ResultToLess_less), .ShiftSrc(Decoder_shiftsrc), .ShifterToReg(Decoder_shiftertoreg),
    .RegWrite(Decoder_regwrite), .ALUOp(Decoder_aluop), .IMMtoALU(Decoder_immtoalu),
    .RegtoPC(Decoder_regtopc), .IMMtoPC(Decoder_immtopc), .MemWrite(Decoder_memwrite),
    .ZerosToALU(Decoder_zerostoalu), .MemtoReg(Decoder_memtoreg), .Halt(Decoder_halt), .LED(Decoder_led),
    .WriteLED(Decoder_writeled), .MemRead(Decoder_memread), .PCtoReg(Decoder_pctoreg));
  Register_File Registers_File (
    .Read_Register1(Instruction_Splitter_read_register1),
    .Read_Register2(Instruction_Splitter_read_register2), .Write_Data(multiplexer_5_out),
    .Write_Enable(Decoder_regwrite), .Clock(clock_1_out), .Read_Data1(Registers_File_read_data1),
    .Read_Data2(Registers_File_read_data2));  // open: Write_Register
  ID_EX_Buffer ID_EX (
    .AluOP(Decoder_aluop), .SubOp(Instruction_Splitter_subop), .ReadData1(Registers_File_read_data1),
    .Shamt(Instruction_Splitter_shift_amount), .ReadData2(Registers_File_read_data2),
    .IMM_ext(Sign_Extend_sign_extended_imm), .MemWrite(Decoder_memwrite), .MemRead(Decoder_memread),
    .PC_Plus1(IF_ID_pc_out), .WriteReg(Instruction_Splitter_write_register), .Clock(clock_1_out),
    .ALUOp_2(ID_EX_aluop_2), .SubOp_2(ID_EX_subop_2), .ReadData1_2(ID_EX_readdata1_2),
    .Shamt_2(ID_EX_shamt_2), .ReadData2_2(ID_EX_readdata2_2), .IMM_ext_2(ID_EX_imm_ext_2),
    .MemWrite_2(ID_EX_memwrite_2), .MemRead_2(ID_EX_memread_2));  // open: EX_CTRL, WB_CTRL, Rt, Bubble, EX_CTRL_2, PC_Plus1_2, WriteReg_2, WB_CTRL_2, Rt_2
  ALUtoPC RegisterToAddress (.ALUOut(ID_EX_readdata1_2), .Address(RegisterToAddress_address));
  Multiplexer #(.width(16), .disabled(0), .enable("false")) multiplexer_1 (
    .in0(ID_EX_readdata2_2), .in1(ID_EX_imm_ext_2), .out(multiplexer_1_out), .sel(Decoder_immtoalu));
  Multiplexer #(.width(16), .disabled(0), .enable("false")) multiplexer_2 (
    .in0(multiplexer_1_out), .in1({16{1'b0}}), .out(multiplexer_2_out), .sel(ID_EX_memwrite_2));
  Multiplexer #(.width(8), .disabled(0), .enable("false")) multiplexer_3 (
    .in0(adder_1_out), .in1(Instruction_Splitter_immediate), .out(multiplexer_3_out), .sel(Decoder_immtopc));
  sixteenBit_ALU ALU (
    .ALUOperation(ID_EX_aluop_2), .A(ID_EX_readdata1_2), .B(multiplexer_2_out), .Zero(ALU_zero),
    .Result(ALU_result));  // open: Overflow
  Multiplexer #(.width(8), .disabled(0), .enable("false")) multiplexer_4 (
    .in0(multiplexer_3_out), .in1(RegisterToAddress_address), .out(multiplexer_4_out), .sel(Decoder_regtopc));
  Shifter Shifter (
    .Subop(ID_EX_subop_2), .Data(ID_EX_readdata1_2), .ShamtReg(ID_EX_readdata2_2),
    .ShiftSrc(Decoder_shiftsrc), .Shamt(ID_EX_shamt_2), .ShiftOut(Shifter_shiftout));
  assign bit_extender_1_out = {{8{1'b0}}, adder_1_out};  // Bit_Extender bit_extender_1
  ALUtoPC RegisterToAddress_2 (.ALUOut(ID_EX_readdata2_2), .Address(RegisterToAddress_2_address));
  Multiplexer #(.width(16), .disabled(0), .enable("false")) multiplexer_5 (
    .in0(multiplexer_6_out), .in1(bit_extender_1_out), .out(multiplexer_5_out), .sel(Decoder_pctoreg));
  RAM #(.dataWidth(16), .bus("separate")) ram_1 (
    .addr(RegisterToAddress_2_address), .din(ID_EX_readdata1_2), .data(ram_1_data), .str(Decoder_zerostoalu),
    .sel(1'b1), .clk(clock_1_out), .ld(ID_EX_memread_2));  // open: clr
  Multiplexer #(.width(16), .disabled(0), .enable("false")) multiplexer_6 (
    .in0(multiplexer_7_out), .in1(Shifter_shiftout), .out(multiplexer_6_out), .sel(Decoder_shiftertoreg));
  Register #(.width(16)) register_1 (
    .D(ID_EX_readdata1_2), .en(Decoder_writeled), .Q(register_1_q), .clk(clock_1_out));  // open: clr
  LED Halt (.in(Decoder_led));
  Multiplexer #(.width(16), .disabled(0), .enable("false")) multiplexer_7 (
    .in0(ALU_result), .in1(ram_1_data), .out(multiplexer_7_out), .sel(Decoder_memtoreg));
  Hex_Digit_Display hex_digit_display_1 (.value(register_1_q[15:12]));  // open: dp
  Hex_Digit_Display hex_digit_display_2 (.value(register_1_q[11:8]));  // open: dp
  Hex_Digit_Display hex_digit_display_3 (.value(register_1_q[3:0]));  // open: dp
  Hex_Digit_Display hex_digit_display_4 (.value(register_1_q[7:4]));  // open: dp
endmodule

module Instruction_Splitter (
  input  [15:0] Instruction,
  output [3:0] Opcode,
  output [2:0] Read_Register1,
  output [2:0] Read_Register2,
  output [2:0] Write_Register,
  output [3:0] Shift_Amount,
  output SubOp,
  output Unsigned,
  output [7:0] Immediate
);


  assign Immediate = Instruction[7:0];
  assign Opcode = Instruction[15:12];
  assign Read_Register1 = Instruction[11:9];
  assign Read_Register2 = Instruction[8:6];
  assign Shift_Amount = Instruction[4:1];
  assign SubOp = Instruction[0];
  assign Unsigned = Instruction[8];
  assign Write_Register = Instruction[11:9];
endmodule

module Sign_Extend (
  input  Unsigned,
  input  [7:0] Immediate,
  output [15:0] Sign_Extended_Imm
);

  wire [15:0] bit_extender_1_out, bit_extender_2_out;

  assign bit_extender_1_out = {{8{Immediate[7]}}, Immediate};  // Bit_Extender bit_extender_1
  assign bit_extender_2_out = {{8{1'b0}}, Immediate};  // Bit_Extender bit_extender_2
  Multiplexer #(.width(16), .disabled(0), .enable("false")) multiplexer_1 (
    .in0(bit_extender_1_out), .in1(bit_extender_2_out), .out(Sign_Extended_Imm), .sel(Unsigned));
endmodule

module Register_File (
  input  [2:0] Read_Register1,
  input  [2:0] Read_Register2,
  input  [2:0] Write_Register,
  input  [15:0] Write_Data,
  input  Write_Enable,
  input  Clock,
  output [15:0] Read_Data1,
  output [15:0] Read_Data2
);

  wire decoder_1_out0, decoder_1_out1, decoder_1_out2, decoder_1_out3, decoder_1_out4, decoder_1_out5,
       decoder_1_out6, decoder_1_out7;
  wire [15:0] R0_q, R1_q, R2_q, R3_q, R4_q, R5_q, R6_q, R7_q;

  Decoder_part #(.select(3), .disabled(0)) decoder_1 (
    .out0(decoder_1_out0), .out1(decoder_1_out1), .out2(decoder_1_out2), .out3(decoder_1_out3),
    .out4(decoder_1_out4), .out5(decoder_1_out5), .out6(decoder_1_out6), .out7(decoder_1_out7),
    .sel(Write_Register), .en(Write_Enable));
  Register #(.width(16)) R0 (.D(Write_Data), .en(decoder_1_out0), .Q(R0_q), .clk(Clock));  // open: clr
  Register #(.width(16)) R1 (.D(Write_Data), .en(decoder_1_out1), .Q(R1_q), .clk(Clock));  // open: clr
  Register #(.width(16)) R2 (.D(Write_Data), .en(decoder_1_out2), .Q(R2_q), .clk(Clock));  // open: clr
  Register #(.width(16)) R3 (.D(Write_Data), .en(decoder_1_out3), .Q(R3_q), .clk(Clock));  // open: clr
  Register #(.width(16)) R4 (.D(Write_Data), .en(decoder_1_out4), .Q(R4_q), .clk(Clock));  // open: clr
  Register #(.width(16)) R5 (.D(Write_Data), .en(decoder_1_out5), .Q(R5_q), .clk(Clock));  // open: clr
  Register #(.width(16)) R6 (.D(Write_Data), .en(decoder_1_out6), .Q(R6_q), .clk(Clock));  // open: clr
  Register #(.width(16)) R7 (.D(Write_Data), .en(decoder_1_out7), .Q(R7_q), .clk(Clock));  // open: clr
  Multiplexer #(.select(3), .width(16), .enable("false")) multiplexer_1 (
    .in0(R0_q), .in1(R1_q), .in2(R2_q), .in3(R3_q), .in4(R4_q), .in5(R5_q), .in6(R6_q), .in7(R7_q),
    .out(Read_Data1), .sel(Read_Register1));
  Multiplexer #(.select(3), .width(16), .enable("false")) multiplexer_2 (
    .in0(R0_q), .in1(R1_q), .in2(R2_q), .in3(R3_q), .in4(R4_q), .in5(R5_q), .in6(R6_q), .in7(R7_q),
    .out(Read_Data2), .sel(Read_Register2));
endmodule

module ALUtoPC (
  input  [15:0] ALUOut,
  output [7:0] Address
);


  assign Address = ALUOut[7:0];
endmodule

module sixteenBit_ALU (
  input  [3:0] ALUOperation,
  input  [15:0] A,
  input  [15:0] B,
  output Zero,
  output [15:0] Result,
  output Overflow
);

  wire one_bit_alu_1_carryout, one_bit_alu_2_carryout, one_bit_alu_3_carryout, one_bit_alu_4_carryout,
       one_bit_alu_5_carryout, one_bit_alu_6_carryout, one_bit_alu_7_carryout, one_bit_alu_8_carryout,
       one_bit_alu_9_carryout, one_bit_alu_10_carryout, one_bit_alu_11_carryout, one_bit_alu_12_carryout,
       one_bit_alu_13_carryout, one_bit_alu_14_carryout, one_bit_alu_15_carryout, one_bit_alu_16_carryout,
       one_bit_alu_16_set, xor_1_out;

  one_bit_ALU one_bit_alu_1 (
    .a(A[0]), .b(B[0]), .Less(xor_1_out), .Ainvert(ALUOperation[3]), .Binvert(ALUOperation[2]),
    .CarryIn(ALUOperation[2]), .Operation(ALUOperation[1:0]), .CarryOut(one_bit_alu_1_carryout),
    .Result(Result[0]));  // open: Set
  one_bit_ALU one_bit_alu_2 (
    .a(A[1]), .b(B[1]), .Less(1'b0), .Ainvert(ALUOperation[3]), .Binvert(ALUOperation[2]),
    .CarryIn(one_bit_alu_1_carryout), .Operation(ALUOperation[1:0]), .CarryOut(one_bit_alu_2_carryout),
    .Result(Result[1]));  // open: Set
  one_bit_ALU one_bit_alu_3 (
    .a(A[2]), .b(B[2]), .Less(1'b0), .Ainvert(ALUOperation[3]), .Binvert(ALUOperation[2]),
    .CarryIn(one_bit_alu_2_carryout), .Operation(ALUOperation[1:0]), .CarryOut(one_bit_alu_3_carryout),
    .Result(Result[2]));  // open: Set
  one_bit_ALU one_bit_alu_4 (
    .a(A[3]), .b(B[3]), .Less(1'b0), .Ainvert(ALUOperation[3]), .Binvert(ALUOperation[2]),
    .CarryIn(one_bit_alu_3_carryout), .Operation(ALUOperation[1:0]), .CarryOut(one_bit_alu_4_carryout),
    .Result(Result[3]));  // open: Set
  one_bit_ALU one_bit_alu_5 (
    .a(A[4]), .b(B[4]), .Less(1'b0), .Ainvert(ALUOperation[3]), .Binvert(ALUOperation[2]),
    .CarryIn(one_bit_alu_4_carryout), .Operation(ALUOperation[1:0]), .CarryOut(one_bit_alu_5_carryout),
    .Result(Result[4]));  // open: Set
  one_bit_ALU one_bit_alu_6 (
    .a(A[5]), .b(B[5]), .Less(1'b0), .Ainvert(ALUOperation[3]), .Binvert(ALUOperation[2]),
    .CarryIn(one_bit_alu_5_carryout), .Operation(ALUOperation[1:0]), .CarryOut(one_bit_alu_6_carryout),
    .Result(Result[5]));  // open: Set
  one_bit_ALU one_bit_alu_7 (
    .a(A[6]), .b(B[6]), .Less(1'b0), .Ainvert(ALUOperation[3]), .Binvert(ALUOperation[2]),
    .CarryIn(one_bit_alu_6_carryout), .Operation(ALUOperation[1:0]), .CarryOut(one_bit_alu_7_carryout),
    .Result(Result[6]));  // open: Set
  one_bit_ALU one_bit_alu_8 (
    .a(A[7]), .b(B[7]), .Less(1'b0), .Ainvert(ALUOperation[3]), .Binvert(ALUOperation[2]),
    .CarryIn(one_bit_alu_7_carryout), .Operation(ALUOperation[1:0]), .CarryOut(one_bit_alu_8_carryout),
    .Result(Result[7]));  // open: Set
  one_bit_ALU one_bit_alu_9 (
    .a(A[8]), .b(B[8]), .Less(1'b0), .Ainvert(ALUOperation[3]), .Binvert(ALUOperation[2]),
    .CarryIn(one_bit_alu_8_carryout), .Operation(ALUOperation[1:0]), .CarryOut(one_bit_alu_9_carryout),
    .Result(Result[8]));  // open: Set
  one_bit_ALU one_bit_alu_10 (
    .a(A[9]), .b(B[9]), .Less(1'b0), .Ainvert(ALUOperation[3]), .Binvert(ALUOperation[2]),
    .CarryIn(one_bit_alu_9_carryout), .Operation(ALUOperation[1:0]), .CarryOut(one_bit_alu_10_carryout),
    .Result(Result[9]));  // open: Set
  one_bit_ALU one_bit_alu_11 (
    .a(A[10]), .b(B[10]), .Less(1'b0), .Ainvert(ALUOperation[3]), .Binvert(ALUOperation[2]),
    .CarryIn(one_bit_alu_10_carryout), .Operation(ALUOperation[1:0]), .CarryOut(one_bit_alu_11_carryout),
    .Result(Result[10]));  // open: Set
  one_bit_ALU one_bit_alu_12 (
    .a(A[11]), .b(B[11]), .Less(1'b0), .Ainvert(ALUOperation[3]), .Binvert(ALUOperation[2]),
    .CarryIn(one_bit_alu_11_carryout), .Operation(ALUOperation[1:0]), .CarryOut(one_bit_alu_12_carryout),
    .Result(Result[11]));  // open: Set
  one_bit_ALU one_bit_alu_13 (
    .a(A[12]), .b(B[12]), .Less(1'b0), .Ainvert(ALUOperation[3]), .Binvert(ALUOperation[2]),
    .CarryIn(one_bit_alu_12_carryout), .Operation(ALUOperation[1:0]), .CarryOut(one_bit_alu_13_carryout),
    .Result(Result[12]));  // open: Set
  one_bit_ALU one_bit_alu_14 (
    .a(A[13]), .b(B[13]), .Less(1'b0), .Ainvert(ALUOperation[3]), .Binvert(ALUOperation[2]),
    .CarryIn(one_bit_alu_13_carryout), .Operation(ALUOperation[1:0]), .CarryOut(one_bit_alu_14_carryout),
    .Result(Result[13]));  // open: Set
  one_bit_ALU one_bit_alu_15 (
    .a(A[14]), .b(B[14]), .Less(1'b0), .Ainvert(ALUOperation[3]), .Binvert(ALUOperation[2]),
    .CarryIn(one_bit_alu_14_carryout), .Operation(ALUOperation[1:0]), .CarryOut(one_bit_alu_15_carryout),
    .Result(Result[14]));  // open: Set
  one_bit_ALU one_bit_alu_16 (
    .a(A[15]), .b(B[15]), .Ainvert(ALUOperation[3]), .Binvert(ALUOperation[2]),
    .CarryIn(one_bit_alu_15_carryout), .Operation(ALUOperation[1:0]), .CarryOut(one_bit_alu_16_carryout),
    .Result(Result[15]), .Set(one_bit_alu_16_set));  // open: Less
  xor xor_1 (xor_1_out, one_bit_alu_16_set, Overflow);
  xor xor_2 (Overflow, one_bit_alu_15_carryout, one_bit_alu_16_carryout);
  nor nor_1 (Zero, Result[0], Result[1], Result[2], Result[3], Result[4], Result[5], Result[6], Result[7], Result[8], Result[9], Result[10], Result[11], Result[12], Result[13], Result[14], Result[15]);
endmodule

module one_bit_ALU (
  input  CarryIn,
  input  [1:0] Operation,
  input  Ainvert,
  input  Binvert,
  input  a,
  input  b,
  input  Less,
  output Result,
  output Set,
  output CarryOut
);

  wire and_1_out, multiplexer_1_out, multiplexer_2_out, not_1_out, not_2_out, or_1_out;

  not not_1 (not_1_out, a);
  Multiplexer #(.enable("false")) multiplexer_1 (.in0(a), .in1(not_1_out), .out(multiplexer_1_out), .sel(Ainvert));
  Multiplexer #(.enable("false")) multiplexer_2 (.in0(b), .in1(not_2_out), .out(multiplexer_2_out), .sel(Binvert));
  not not_2 (not_2_out, b);
  and and_1 (and_1_out, multiplexer_1_out, multiplexer_2_out);
  or or_1 (or_1_out, multiplexer_1_out, multiplexer_2_out);
  Adder #(.width(1)) adder_1 (.a(multiplexer_1_out), .b(multiplexer_2_out), .out(Set), .cin(CarryIn), .cout(CarryOut));
  Multiplexer #(.select(2), .enable("false")) multiplexer_3 (
    .in0(and_1_out), .in1(or_1_out), .in2(Set), .in3(Less), .out(Result), .sel(Operation));
endmodule

module ResultToLess (
  input  [15:0] Result,
  output Less
);


  assign Less = Result[15];
endmodule

module Decoder (
  input  [3:0] Opcode,
  input  SubOp,
  input  Zero,
  input  Less,
  output ShiftSrc,
  output ShifterToReg,
  output RegWrite,
  output [3:0] ALUOp,
  output IMMtoALU,
  output RegtoPC,
  output IMMtoPC,
  output MemWrite,
  output ZerosToALU,
  output MemtoReg,
  output Halt,
  output LED,
  output WriteLED,
  output MemRead,
  output PCtoReg
);

  wire Arith_Log_Decoder_regwrite, JALDecoder_immtopc, JALDecoder_regwrite, MemDecoder_regwrite,
       PCDecoder_immtopc, ShifterDecoder_regwrite;
  wire [3:0] Arith_Log_Decoder_aluoperation, PCDecoder_aluop;

  ShifterDecoder ShifterDecoder (
    .Opcode(Opcode), .ShiftSrc(ShiftSrc), .ShifterToReg(ShifterToReg), .RegWrite(ShifterDecoder_regwrite));
  Arith_Log_Decoder Arith_Log_Decoder (
    .Opcode(Opcode), .SubOp(SubOp), .ALUOperation(Arith_Log_Decoder_aluoperation),
    .RegWrite(Arith_Log_Decoder_regwrite), .ALUsrc(IMMtoALU));
  PCDecoder PCDecoder (
    .Opcode(Opcode), .Subop(SubOp), .Zero(Zero), .Less(Less), .RegtoPC(RegtoPC), .IMMtoPC(PCDecoder_immtopc),
    .ZerosToALU(ZerosToALU), .ALUOp(PCDecoder_aluop));
  MemDecoder MemDecoder (
    .Opcode(Opcode), .Subop(SubOp), .MemWrite(MemWrite), .MemtoReg(MemtoReg), .RegWrite(MemDecoder_regwrite),
    .MemRead(MemRead));
  HaltDecoder HaltDecoder (.Opcode(Opcode), .Halt(Halt), .LED(LED));
  PutDecoder PutDecoder (.Opcode(Opcode), .WriteLED(WriteLED));
  JALDecoder JALDecoder (
    .Opcode(Opcode), .IMMtoPC(JALDecoder_immtopc), .PCtoReg(PCtoReg), .RegWrite(JALDecoder_regwrite));
  or or_1 (RegWrite, ShifterDecoder_regwrite, Arith_Log_Decoder_regwrite, MemDecoder_regwrite, JALDecoder_regwrite);
  or or_2 (IMMtoPC, PCDecoder_immtopc, JALDecoder_immtopc);
  assign ALUOp = Arith_Log_Decoder_aluoperation | PCDecoder_aluop;  // OR_Gate or_3, 4 bits wide
endmodule

module ShifterDecoder (
  input  [3:0] Opcode,
  output ShiftSrc,
  output ShifterToReg,
  output RegWrite
);

  and and_1 (RegWrite, Opcode[3], Opcode[2], Opcode[1]);

  assign ShifterToReg = RegWrite;
  assign ShiftSrc = Opcode[0];
endmodule

module Arith_Log_Decoder (
  input  [3:0] Opcode,
  input  SubOp,
  output [3:0] ALUOperation,
  output RegWrite,
  output ALUsrc
);

  wire and_2_out, and_3_out, and_5_out, and_6_out, not_1_out, not_2_out, not_3_out, not_4_out, not_5_out,
       not_6_out, not_7_out, not_8_out, not_9_out, not_10_out, not_11_out, not_12_out, not_13_out,
       not_14_out, not_15_out, not_16_out, not_17_out, not_18_out, not_19_out, not_20_out, not_21_out;

  not not_1 (not_1_out, Opcode[3]);
  not not_2 (not_2_out, Opcode[2]);
  not not_3 (not_3_out, SubOp);
  and and_1 (ALUOperation[3], not_1_out, not_2_out, Opcode[1], Opcode[0], not_3_out);
  not not_4 (not_4_out, Opcode[3]);
  not not_5 (not_5_out, Opcode[2]);
  not not_6 (not_6_out, Opcode[1]);
  and and_2 (and_2_out, not_4_out, not_5_out, not_6_out, not_7_out, SubOp);
  not not_7 (not_7_out, Opcode[0]);
  not not_8 (not_8_out, Opcode[3]);
  not not_9 (not_9_out, Opcode[2]);
  and and_3 (and_3_out, not_8_out, not_9_out, Opcode[1], Opcode[0], not_10_out);
  not not_10 (not_10_out, SubOp);
  not not_11 (not_11_out, Opcode[3]);
  and and_4 (ALUOperation[1], not_11_out, not_12_out, not_13_out);
  not not_12 (not_12_out, Opcode[2]);
  not not_13 (not_13_out, Opcode[1]);
  not not_14 (not_14_out, Opcode[3]);
  not not_15 (not_15_out, Opcode[2]);
  and and_5 (and_5_out, not_14_out, not_15_out, not_16_out);
  not not_16 (not_16_out, Opcode[1]);
  not not_17 (not_17_out, Opcode[3]);
  and and_6 (and_6_out, not_17_out, not_18_out, Opcode[0]);
  not not_18 (not_18_out, Opcode[2]);
  not not_19 (not_19_out, Opcode[3]);
  not not_20 (not_20_out, Opcode[2]);
  and and_7 (ALUsrc, not_19_out, not_20_out, not_21_out, Opcode[0]);
  not not_21 (not_21_out, Opcode[1]);
  or or_1 (RegWrite, and_5_out, and_6_out);
  or or_2 (ALUOperation[2], and_2_out, and_3_out);

  assign ALUOperation[0] = 1'b0;
endmodule

module PCDecoder (
  input  [3:0] Opcode,
  input  Subop,
  input  Zero,
  input  Less,
  output RegtoPC,
  output IMMtoPC,
  output ZerosToALU,
  output [3:0] ALUOp
);

  wire and_2_out, and_3_out, and_4_out, and_5_out, and_6_out, not_1_out, not_2_out, not_3_out, not_4_out,
       not_5_out, not_6_out, not_7_out, not_8_out, not_9_out, not_10_out, not_11_out, not_12_out, not_13_out,
       not_14_out, not_15_out, not_16_out;

  not not_1 (not_1_out, Opcode[1]);
  not not_2 (not_2_out, Subop);
  not not_3 (not_3_out, Opcode[2]);
  not not_4 (not_4_out, Opcode[1]);
  not not_5 (not_5_out, Opcode[0]);
  not not_6 (not_6_out, Opcode[2]);
  not not_7 (not_7_out, Opcode[1]);
  not not_8 (not_8_out, Zero);
  not not_9 (not_9_out, Opcode[2]);
  not not_10 (not_10_out, Zero);
  not not_11 (not_11_out, Opcode[0]);
  not not_12 (not_12_out, Zero);
  not not_13 (not_13_out, Less);
  not not_14 (not_14_out, Opcode[0]);
  not not_15 (not_15_out, Opcode[2]);
  not not_16 (not_16_out, Opcode[2]);
  and and_1 (RegtoPC, Opcode[3], Opcode[2], not_1_out, Opcode[0], not_2_out);
  and and_2 (and_2_out, Opcode[3], not_3_out, not_4_out, not_5_out, Zero);
  and and_3 (and_3_out, Opcode[3], not_6_out, not_7_out, Opcode[0], not_8_out);
  and and_4 (and_4_out, Opcode[3], not_9_out, Opcode[0], not_10_out, Less);
  and and_5 (and_5_out, Opcode[3], Opcode[1], not_11_out, not_12_out, not_13_out);
  and and_6 (and_6_out, Opcode[3], Opcode[2], Opcode[1], not_14_out);
  and and_7 (ZerosToALU, Opcode[3], not_15_out);
  and and_8 (ALUOp[1], Opcode[3], not_16_out);
  or or_1 (IMMtoPC, and_2_out, and_3_out, and_4_out, and_5_out, and_6_out);

  assign {ALUOp[3:2], ALUOp[0]} = 3'b000;
endmodule

module MemDecoder (
  input  [3:0] Opcode,
  input  Subop,
  output MemWrite,
  output MemtoReg,
  output RegWrite,
  output MemRead
);

  and and_1 (MemWrite, Opcode[0], Opcode[1], Opcode[2], Opcode[3], Subop);
  and and_2 (MemRead, Opcode[0], Opcode[1], Opcode[2], Opcode[3], Subop);

  assign MemtoReg = MemRead;
  assign RegWrite = MemRead;
endmodule

module HaltDecoder (
  input  [3:0] Opcode,
  output Halt,
  output LED
);

  and and_1 (Halt, Opcode[3], Opcode[2], Opcode[1], Opcode[0]);

  assign LED = Halt;
endmodule

module PutDecoder (
  input  [3:0] Opcode,
  output WriteLED
);

  and and_1 (WriteLED, Opcode[0], Opcode[1], Opcode[2], Opcode[3]);
endmodule

module JALDecoder (
  input  [3:0] Opcode,
  output IMMtoPC,
  output PCtoReg,
  output RegWrite
);

  and and_1 (IMMtoPC, Opcode[0], Opcode[1], Opcode[2], Opcode[3]);

  assign PCtoReg = IMMtoPC;
  assign RegWrite = IMMtoPC;
endmodule

module Shifter (
  input  Subop,
  input  [15:0] Data,
  input  [15:0] ShamtReg,
  input  ShiftSrc,
  input  [3:0] Shamt,
  output [15:0] ShiftOut
);

  wire [3:0] multiplexer_1_out;
  wire [15:0] shifter_1_out, shifter_2_out;

  Multiplexer #(.width(4), .disabled(0), .enable("false")) multiplexer_1 (
    .in0(ShamtReg[3:0]), .in1(Shamt), .out(multiplexer_1_out), .sel(ShiftSrc));
  Shifter_part #(.width(16)) shifter_1 (.in(Data), .\dist (multiplexer_1_out), .out(shifter_1_out));
  Shifter_part #(.width(16), .shift("lr")) shifter_2 (.in(Data), .\dist (multiplexer_1_out), .out(shifter_2_out));
  Multiplexer #(.width(16), .disabled(0), .enable("false")) multiplexer_2 (
    .in0(shifter_1_out), .in1(shifter_2_out), .out(ShiftOut), .sel(Subop));
endmodule

module IF_ID_Buffer (
  input  [7:0] PC,
  input  [15:0] Input_Instruction,
  input  Clock,
  output [7:0] PC_out,
  output [15:0] Output_Instruction
);

  Register register_1 (.D(PC), .Q(PC_out), .clk(Clock));  // open: en, clr
  Register #(.width(16)) register_2 (.D(Input_Instruction), .Q(Output_Instruction), .clk(Clock));  // open: en, clr
endmodule

module ID_EX_Buffer (
  input  [3:0] AluOP,
  input  SubOp,
  input  [15:0] ReadData1,
  input  [3:0] Shamt,
  input  [15:0] ReadData2,
  input  [15:0] IMM_ext,
  input  [5:0] EX_CTRL,
  input  MemWrite,
  input  MemRead,
  input  [7:0] PC_Plus1,
  input  [2:0] WriteReg,
  input  [5:0] WB_CTRL,
  input  [2:0] Rt,
  input  Bubble,
  input  Clock,
  output [3:0] ALUOp_2,
  output SubOp_2,
  output [15:0] ReadData1_2,
  output [3:0] Shamt_2,
  output [15:0] ReadData2_2,
  output [15:0] IMM_ext_2,
  output [5:0] EX_CTRL_2,
  output MemWrite_2,
  output MemRead_2,
  output [7:0] PC_Plus1_2,
  output [2:0] WriteReg_2,
  output [5:0] WB_CTRL_2,
  output [2:0] Rt_2
);

  wire and_3_out;
  wire [5:0] and_1_out, and_2_out;
  wire [5:5] not_1_out;

  assign and_1_out = WB_CTRL & {6{not_1_out[5]}};  // AND_Gate and_1, 6 bits wide
  not not_1 (not_1_out[5], Bubble);
  Register #(.width(4)) register_1 (.D(AluOP), .Q(ALUOp_2), .clk(Clock));  // open: en, clr
  Register #(.width(1)) register_2 (.D(SubOp), .Q(SubOp_2), .clk(Clock));  // open: en, clr
  Register #(.width(16)) register_3 (.D(ReadData1), .Q(ReadData1_2), .clk(Clock));  // open: en, clr
  Register #(.width(4)) register_4 (.D(Shamt), .Q(Shamt_2), .clk(Clock));  // open: en, clr
  Register #(.width(16)) register_5 (.D(ReadData2), .Q(ReadData2_2), .clk(Clock));  // open: en, clr
  Register #(.width(16)) register_6 (.D(IMM_ext), .Q(IMM_ext_2), .clk(Clock));  // open: en, clr
  assign and_2_out = EX_CTRL & {6{not_1_out[5]}};  // AND_Gate and_2, 6 bits wide
  Register #(.width(6)) register_7 (.D(and_2_out), .Q(EX_CTRL_2), .clk(Clock));  // open: en, clr
  Register #(.width(1)) register_8 (.D(and_3_out), .Q(MemWrite_2), .clk(Clock));  // open: en, clr
  and and_3 (and_3_out, MemWrite, not_1_out[5]);
  Register #(.width(1)) register_9 (.D(MemRead), .Q(MemRead_2), .clk(Clock));  // open: en, clr
  Register register_10 (.D(PC_Plus1), .Q(PC_Plus1_2), .clk(Clock));  // open: en, clr
  Register #(.width(3)) register_11 (.D(WriteReg), .Q(WriteReg_2), .clk(Clock));  // open: en, clr
  Register #(.width(6)) register_12 (.D(and_1_out), .Q(WB_CTRL_2), .clk(Clock));  // open: en, clr
  Register #(.width(3)) register_13 (.D(Rt), .Q(Rt_2), .clr(Clock));  // open: en, clk
endmodule

module EX_MEM_Buffer (
  input  [5:0] WB_CTRL,
  input  [7:0] Adder_Result,
  input  Zero_ALU,
  input  [15:0] Result_ALU,
  input  [15:0] ReadData2,
  input  [2:0] WriteReg,
  input  Bubble,
  input  Clock,
  output [5:0] WB_CTRL_2,
  output [7:0] Adder_Result_2,
  output Zero_ALU_2,
  output [15:0] Result_ALU_2,
  output [15:0] ReadData2_2,
  output [2:0] WriteReg_2
);

  wire [5:0] and_1_out;

  assign and_1_out = WB_CTRL & {6{Bubble}};  // AND_Gate and_1, 6 bits wide
  Register #(.width(6)) register_1 (.D(and_1_out), .Q(WB_CTRL_2), .clk(Clock));  // open: en, clr
  Register register_2 (.D(Adder_Result), .Q(Adder_Result_2), .clk(Clock));  // open: en, clr
  Register #(.width(1)) register_3 (.D(Zero_ALU), .Q(Zero_ALU_2), .clk(Clock));  // open: en, clr
  Register #(.width(16)) register_4 (.D(Result_ALU), .Q(Result_ALU_2), .clk(Clock));  // open: en, clr
  Register #(.width(16)) register_5 (.D(ReadData2), .Q(ReadData2_2), .clk(Clock));  // open: en, clr
  Register #(.width(3)) register_6 (.D(WriteReg), .Q(WriteReg_2), .clk(Clock));  // open: en, clr
endmodule

module Mem_WB_Buffer (
  input  [5:0] WB_CTRL,
  input  [15:0] Data,
  input  [15:0] ReadData2,
  input  [2:0] WriteReg,
  input  Bubble,
  input  Clock,
  output [5:0] WB_CTRL_2,
  output [15:0] Data_2,
  output [15:0] ReadData2_2,
  output [2:0] WriteReg_2
);

  wire [5:0] and_1_out;

  assign and_1_out = WB_CTRL & {6{Bubble}};  // AND_Gate and_1, 6 bits wide
  Register #(.width(6)) register_1 (.D(and_1_out), .Q(WB_CTRL_2), .clk(Clock));  // open: en, clr
  Register #(.width(16)) register_2 (.D(Data), .Q(Data_2), .clk(Clock));  // open: en, clr
  Register #(.width(16)) register_3 (.D(ReadData2), .Q(ReadData2_2));  // open: en, clk, clr
  Register #(.width(3)) register_4 (.D(WriteReg), .Q(WriteReg_2), .clk(Clock));  // open: en, clr
endmodule
